# Fritzing sketch saxelerophone (saved by Fritzing 0.9.3b)
breadboards: 1

parts:
  Bela1 = Bela
  Composant1 = Triple Axis Accelerometer Breakout - ADXL335
  J1 = Piezo Speaker
  R1 = Resistor [tolerance=±5% resistance=330k package=THT]

nets:
  N1: Bela1.P9_01_GND, J1.pin1
  N2: Bela1.P9_02_GND, Composant1.GND
  N3: Bela1.P9_03_3.3V, R1.Pin_0
  N4: Bela1.P9_04_3.3V, Composant1.VCC
  N5: Bela1.AIN_2, Composant1.ZOUT
  N6: Bela1.AIN_1, Composant1.YOUT
  N7: Bela1.AIN_0, Composant1.XOUT
  N8: Bela1.AUDIOIN_L, J1.pin2, R1.Pin_1

notes:
  Piezo microphone connected to bipolar audio ADC
  Resistor is 330kΩ

custom parts:
  Bela: A Fritzing part for Bela
